# Fritzing sketch botanique_wire_diagram (saved by Fritzing 0.9.3b)
breadboards: 1

parts:
  M1 = FireBeetle ESP32-E
  A1 = GY-BMP280 Breakout  # not connected
  A2 = lcd color display 1.3in 240x240 7pin interface [package=THT]
  Capacitive_Soil_Moisture_Sensor1 = DFRobot Capacitive Soil Moisture Sensor V1.0 [part_number=SEN0193]
  S1 = Momentary Switch [package=ksa_sealed_tac_switch]
  R1 = Photocell (LDR) [package=THT]
  R2 = Resistor [tolerance=±5% resistance=220 package=THT]

nets:
  N1: M1.pin_1, A2.RES
  N2: M1.pin_2, M1.pin_3, A2.DC, S1.3
  N3: M1.pin_5, Capacitive_Soil_Moisture_Sensor1.A
  N4: M1.pin_7, R1.pin_0, R2.Pin_1
  N5: M1.pin_9, M1.pin_13, A2.BLK
  GND: M1.pin_12, M1.pin_20, A2.GND, Capacitive_Soil_Moisture_Sensor1.GND
  VCC: M1.pin_14, A2.VCC, Capacitive_Soil_Moisture_Sensor1.VCC, S1.2, R1.pin_1, R2.Pin_0
  N6: M1.pin_21, M1.pin_22, A2.SCL
  N7: M1.pin_23, A2.SDA

custom parts:
  FireBeetle ESP32-E: FireBeetle ESP32-E, specially designed for IoT, is an ESP-WROOM-32E-based main controller board with dual-core chips. It supports WiFi and Bluetooth dual-mode communication and features a small size, ultra-low power consumption, on-board charging circuit, and easy-to-use interface, which can be conveniently used for smart home IoT, industrial IoT applications, wearable devices, and so on. You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
  lcd color display 1.3in 240x240 7pin interface: 1.3 Inch Color 240 x 240 IPS TFT LCD Display Screen Module Board 7 Pin 4 Wire ST7789VW Drive IC SPI interface.
  DFRobot Capacitive Soil Moisture Sensor V1.0: DFRobot Capacitive Soil Moisture Sensor V1.0 This product measures soil moisture levels by capacitive sensing, rather than resistive sensing like other types of moisture sensor. It is made of a corrosion resistant material giving it a long service life. Insert it into soil and impress your friends with the real-time soil moisture data! The product includes an on-board voltage regulator which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
